# Fritzing sketch chicken coop door nano (saved by Fritzing 0.9.3b)
circuit board: 8.46667cm x 5.64444cm
breadboards: 1

parts:
  IC1 = L293D [package=THT]
  R1 = Photocell (LDR) [package=THT]
  R2 = Resistor [tolerance=±5% resistance=15k package=THT]
  M1 = DC Motor
  Part2 = Arduino Nano (Rev3.0)
  BAT1 = BC9VPC [package=bc9vpc]
  12v_1a_power_supply = Power plug

nets:
  N1: IC1.Enable_1, Part2.D11/MOSI
  N2: IC1.In_1, Part2.D10
  GND: IC1.Out_1_(_Controlled_by_Enable_1_), IC1.0V, IC1.Out_2_(_Controlled_by_Enable_1_), R2.Pin_0, M1.pin_1, M1.pin_2, Part2.GND, 12v_1a_power_supply.GND
  N3: IC1.In_2, Part2.D9
  N4: IC1.+Vmotor, 12v_1a_power_supply.VCC
  N5: IC1.+V, R1.pin_1, Part2.5V
  N6: R1.pin_0, R2.Pin_1, Part2.A0
  N7: Part2.VIN, BAT1.V+

// code stored in the sketch: Chicken_door_security_with_power_save.ino
#include "LowPower.h"

int enablePin = 11;
int in1Pin = 10;
int in2Pin = 9;
int switchPin = 7;
const int analogInPin = A0;
const int speed = 128;
boolean direction = true;
boolean prevdirection = false;
int sensorValue = 0;       
//int outputValue = 0;

void setup()
{

  pinMode(in1Pin, OUTPUT);
  pinMode(in2Pin, OUTPUT);
  pinMode(enablePin, OUTPUT);
  pinMode(switchPin, INPUT_PULLUP);
  pinMode(LED_BUILTIN, OUTPUT);
  //Serial.begin (9600);
  
  setMotor(speed, direction);
  delay(3000);
  setMotor(0, direction);
  delay(3000);
}

void loop()
{
   //LowPower.powerDown(SLEEP_8S, ADC_ON, BOD_ON); 
    
     LowPower.idle(SLEEP_8S, ADC_OFF, TIMER2_OFF, TIMER1_OFF, TIMER0_OFF, 
                SPI_OFF, USART0_OFF, TWI_OFF);

   delay(20);
   
   sensorValue = analogRead(analogInPin);

  digitalWrite(LED_BUILTIN, HIGH);   // turn the LED on (HIGH is the voltage level)
  delay(1000);                       // wait for a second
  digitalWrite(LED_BUILTIN, LOW);    // turn the LED off by making the voltage LOW
  delay(1000); 
  
    //Serial.print("sensor = ");
  //Serial.println(sensorValue);

  
  //if it is daylight, & the last action is NOT opening, open the door
if (sensorValue >= 350 && prevdirection == direction){
  
  setMotor(speed, direction);
  delay(3000);
  setMotor(0, direction);
  delay(3000);
  //switch direction
  direction = ! direction;

}
//if it is night, & the last action is NOT closing, close the door
if (sensorValue <= 350 && prevdirection != direction){
  
    setMotor(speed, direction);
  delay(3000);
  setMotor(0, direction);
  delay(3000);
//switch direction
direction = ! direction;

}
 
}

void setMotor(int speed, boolean direction)
{
  analogWrite(enablePin, speed);
  digitalWrite(in1Pin, ! direction);
  digitalWrite(in2Pin, direction);
}
