# Fritzing sketch schematics (saved by Fritzing 0.9.2b)
breadboards: 1

parts:
  Part1 = Arduino Nano (Rev3.0)
  R1 = Resistor [tolerance=±5% resistance=2.2k package=THT]
  R3 = Resistor [tolerance=±5% resistance=2.2k package=THT]
  R4 = Resistor [tolerance=±5% resistance=2.2k package=THT]
  S1 = Pushbutton [package=THT]
  S2 = Pushbutton [package=THT]
  IC2 = L293D [package=THT]
  M1 = DC Motor
  R5 = Photocell (LDR) [package=THT]
  VCC1 = Battery block 9V

nets:
  N1: Part1.GND, R1.Pin_1, R3.Pin_1, R4.Pin_1, IC2.0V, VCC1.-
  N2: Part1.D2, R3.Pin_0, S2.leg1
  N3: Part1.D3, R4.Pin_0, S1.leg1
  N4: Part1.D9, IC2.In_2
  N5: Part1.D10, IC2.In_1
  N6: Part1.5V, S1.leg0, S2.leg0, IC2.Enable_1, IC2.+V, R5.pin_1
  N7: Part1.A0, R1.Pin_0, R5.pin_0
  N8: IC2.Out_1_(_Controlled_by_Enable_1_), M1.pin_2
  N9: IC2.Out_2_(_Controlled_by_Enable_1_), M1.pin_1
  N10: IC2.+Vmotor, VCC1.+
